// Logisim project drawer.circ as structural Verilog: 2 circuits, main circuit using
module using (
  input  [15:0] in_1
);

  wire button_1_out, button_2_out, button_3_out, button_4_out;
  wire [15:0] drawer_1_out_6, drawer_1_out_7, drawer_1_out_8, drawer_1_out_9, drawer_1_out_10,
       drawer_1_out_11, drawer_1_out_12, drawer_1_out_13, drawer_1_out_14, drawer_1_out_15, drawer_1_out_16,
       drawer_1_out_17, drawer_1_out_18, drawer_1_out_19, drawer_1_out_20, drawer_1_out_21;

  Button button_1 (.out(button_1_out));
  Button button_2 (.out(button_2_out));
  Button button_3 (.out(button_3_out));
  Button button_4 (.out(button_4_out));
  drawer drawer_1 (
    .in_3(in_1), .out_6(drawer_1_out_6), .out_7(drawer_1_out_7), .out_8(drawer_1_out_8),
    .out_9(drawer_1_out_9), .out_10(drawer_1_out_10), .out_11(drawer_1_out_11), .out_12(drawer_1_out_12),
    .out_13(drawer_1_out_13), .out_14(drawer_1_out_14), .out_15(drawer_1_out_15), .out_16(drawer_1_out_16),
    .out_17(drawer_1_out_17), .out_18(drawer_1_out_18), .out_19(drawer_1_out_19), .out_20(drawer_1_out_20),
    .out_21(drawer_1_out_21), .clear(button_4_out), .draw(button_1_out), .up(button_2_out),
    .down(button_3_out));
  DotMatrix #(.inputtype("row"), .matrixcols(16), .matrixrows(16)) dotmatrix_1 (
    .row0(drawer_1_out_6), .row1(drawer_1_out_7), .row2(drawer_1_out_8), .row3(drawer_1_out_9),
    .row4(drawer_1_out_10), .row5(drawer_1_out_11), .row6(drawer_1_out_12), .row7(drawer_1_out_13),
    .row8(drawer_1_out_14), .row9(drawer_1_out_15), .row10(drawer_1_out_16), .row11(drawer_1_out_17),
    .row12(drawer_1_out_18), .row13(drawer_1_out_19), .row14(drawer_1_out_20), .row15(drawer_1_out_21));
endmodule

module drawer (
  input  draw,
  input  clear,
  input  [15:0] in_3,
  input  up,
  input  down,
  output [15:0] out_6,
  output [15:0] out_7,
  output [15:0] out_8,
  output [15:0] out_9,
  output [15:0] out_10,
  output [15:0] out_11,
  output [15:0] out_12,
  output [15:0] out_13,
  output [15:0] out_14,
  output [15:0] out_15,
  output [15:0] out_16,
  output [15:0] out_17,
  output [15:0] out_18,
  output [15:0] out_19,
  output [15:0] out_20,
  output [15:0] out_21
);

  wire and_1_out, and_2_out, and_3_out, and_4_out, and_5_out, and_6_out, and_7_out, and_8_out, and_9_out,
       and_10_out, and_11_out, and_12_out, and_13_out, and_14_out, and_15_out, and_16_out, and_17_out,
       and_18_out, and_19_out, and_20_out, and_21_out, and_22_out, and_23_out, and_24_out, and_25_out,
       and_26_out, and_27_out, and_28_out, and_29_out, and_30_out, and_31_out, and_32_out, clock_1_out,
       d_ff_1_q, or_1_out, \й0 , \й1 , \й2 , \й3 , \й4 , \й5 , \й6 , \й7 , \й8 , \й9 , \й10 , \й11 , \й12 ,
       \й13 , \й14 , \й15 ;
  wire [3:0] adder_1_out, multiplexer_1_out, register_1_q, subtractor_1_out;
  wire [15:0] _0, _1, _2, _3, _4, _5, _6, _7, _8, _9, _10, _11, _12, _13, _14, _15, demultiplexer_1_out0,
       demultiplexer_1_out1, demultiplexer_1_out2, demultiplexer_1_out3, demultiplexer_1_out4,
       demultiplexer_1_out5, demultiplexer_1_out6, demultiplexer_1_out7, demultiplexer_1_out8,
       demultiplexer_1_out9, demultiplexer_1_out10, demultiplexer_1_out11, demultiplexer_1_out12,
       demultiplexer_1_out13, demultiplexer_1_out14, demultiplexer_1_out15, not_1_out, register_18_q,
       register_19_q, register_20_q, register_21_q, register_22_q, register_23_q, register_24_q,
       register_25_q, register_26_q, register_27_q, register_28_q, register_29_q, register_30_q,
       register_31_q, register_32_q, register_33_q;

  Subtractor #(.width(4)) subtractor_1 (.a(register_1_q), .b(4'b0001), .out(subtractor_1_out));  // open: bin, bout
  Adder #(.width(4)) adder_1 (.a(register_1_q), .b(4'b0001), .out(adder_1_out));  // open: cin, cout
  D_Flip_Flop d_ff_1 (.Q(d_ff_1_q), .preset(up), .reset(down));  // open: clk, D, Qn, en
  assign not_1_out = ~in_3;  // NOT_Gate not_1, 16 bits wide
  Multiplexer #(.width(4), .enable("false")) multiplexer_1 (
    .in0(adder_1_out), .in1(subtractor_1_out), .out(multiplexer_1_out), .sel(d_ff_1_q));
  Register #(.width(4), .trigger("falling")) register_1 (
    .D(multiplexer_1_out), .Q(register_1_q), .clk(or_1_out));  // open: en, clr
  or or_1 (or_1_out, up, down);
  Demultiplexer #(.select(4), .width(16), .enable("false")) demultiplexer_1 (
    .out0(demultiplexer_1_out0), .out1(demultiplexer_1_out1), .out2(demultiplexer_1_out2),
    .out3(demultiplexer_1_out3), .out4(demultiplexer_1_out4), .out5(demultiplexer_1_out5),
    .out6(demultiplexer_1_out6), .out7(demultiplexer_1_out7), .out8(demultiplexer_1_out8),
    .out9(demultiplexer_1_out9), .out10(demultiplexer_1_out10), .out11(demultiplexer_1_out11),
    .out12(demultiplexer_1_out12), .out13(demultiplexer_1_out13), .out14(demultiplexer_1_out14),
    .out15(demultiplexer_1_out15), .in(not_1_out), .sel(register_1_q));
  and and_1 (and_1_out, draw, \й0 );
  and and_2 (and_2_out, draw, \й1 );
  and and_3 (and_3_out, draw, \й2 );
  and and_4 (and_4_out, draw, \й3 );
  and and_5 (and_5_out, draw, \й4 );
  and and_6 (and_6_out, draw, \й5 );
  and and_7 (and_7_out, draw, \й6 );
  and and_8 (and_8_out, draw, \й7 );
  and and_9 (and_9_out, draw, \й8 );
  and and_10 (and_10_out, draw, \й9 );
  and and_11 (and_11_out, draw, \й10 );
  and and_12 (and_12_out, draw, \й11 );
  and and_13 (and_13_out, draw, \й12 );
  and and_14 (and_14_out, draw, \й13 );
  and and_15 (and_15_out, draw, \й14 );
  and and_16 (and_16_out, draw, \й15 );
  Register #(.width(16)) register_2 (.D(in_3), .en(and_1_out), .Q(_0), .clk(and_1_out), .clr(clear));
  Register #(.width(16)) register_3 (.D(in_3), .en(and_2_out), .Q(_1), .clk(and_2_out), .clr(clear));
  Register #(.width(16)) register_4 (.D(in_3), .en(and_3_out), .Q(_2), .clk(and_3_out), .clr(clear));
  Register #(.width(16)) register_5 (.D(in_3), .en(and_4_out), .Q(_3), .clk(and_4_out), .clr(clear));
  Register #(.width(16)) register_6 (.D(in_3), .en(and_5_out), .Q(_4), .clk(and_5_out), .clr(clear));
  Register #(.width(16)) register_7 (.D(in_3), .en(and_6_out), .Q(_5), .clk(and_6_out), .clr(clear));
  Register #(.width(16)) register_8 (.D(in_3), .en(and_7_out), .Q(_6), .clk(and_7_out), .clr(clear));
  Register #(.width(16)) register_9 (.D(in_3), .en(and_8_out), .Q(_7), .clk(and_8_out), .clr(clear));
  Register #(.width(16)) register_10 (.D(in_3), .en(and_9_out), .Q(_8), .clk(and_9_out), .clr(clear));
  Register #(.width(16)) register_11 (.D(in_3), .en(and_10_out), .Q(_9), .clk(and_10_out), .clr(clear));
  Register #(.width(16)) register_12 (.D(in_3), .en(and_11_out), .Q(_10), .clk(and_11_out), .clr(clear));
  Register #(.width(16)) register_13 (.D(in_3), .en(and_12_out), .Q(_11), .clk(and_12_out), .clr(clear));
  Register #(.width(16)) register_14 (.D(in_3), .en(and_13_out), .Q(_12), .clk(and_13_out), .clr(clear));
  Register #(.width(16)) register_15 (.D(in_3), .en(and_14_out), .Q(_13), .clk(and_14_out), .clr(clear));
  Register #(.width(16)) register_16 (.D(in_3), .en(and_15_out), .Q(_14), .clk(and_15_out), .clr(clear));
  Register #(.width(16)) register_17 (.D(in_3), .en(and_16_out), .Q(_15), .clk(and_16_out), .clr(clear));
  Demultiplexer #(.select(4), .enable("false")) demultiplexer_2 (
    .out0(\й0 ), .out1(\й1 ), .out2(\й2 ), .out3(\й3 ), .out4(\й4 ), .out5(\й5 ), .out6(\й6 ), .out7(\й7 ),
    .out8(\й8 ), .out9(\й9 ), .out10(\й10 ), .out11(\й11 ), .out12(\й12 ), .out13(\й13 ), .out14(\й14 ),
    .out15(\й15 ), .in(1'b1), .sel(register_1_q));
  Clock clock_1 (.out(clock_1_out));
  and and_17 (and_17_out, \й0 , clock_1_out);
  and and_18 (and_18_out, \й1 , clock_1_out);
  and and_19 (and_19_out, \й2 , clock_1_out);
  and and_20 (and_20_out, \й3 , clock_1_out);
  and and_21 (and_21_out, \й4 , clock_1_out);
  and and_22 (and_22_out, \й5 , clock_1_out);
  and and_23 (and_23_out, \й6 , clock_1_out);
  and and_24 (and_24_out, \й7 , clock_1_out);
  and and_25 (and_25_out, \й8 , clock_1_out);
  and and_26 (and_26_out, \й9 , clock_1_out);
  and and_27 (and_27_out, \й10 , clock_1_out);
  and and_28 (and_28_out, \й11 , clock_1_out);
  and and_29 (and_29_out, \й12 , clock_1_out);
  and and_30 (and_30_out, \й13 , clock_1_out);
  and and_31 (and_31_out, \й14 , clock_1_out);
  and and_32 (and_32_out, \й15 , clock_1_out);
  Register #(.width(16)) register_18 (
    .D(demultiplexer_1_out0), .en(\й0 ), .Q(register_18_q), .clk(and_17_out), .clr(clear));
  Register #(.width(16)) register_19 (
    .D(demultiplexer_1_out1), .en(\й1 ), .Q(register_19_q), .clk(and_18_out), .clr(clear));
  Register #(.width(16)) register_20 (
    .D(demultiplexer_1_out2), .en(\й2 ), .Q(register_20_q), .clk(and_19_out), .clr(clear));
  Register #(.width(16)) register_21 (
    .D(demultiplexer_1_out3), .en(\й3 ), .Q(register_21_q), .clk(and_20_out), .clr(clear));
  Register #(.width(16)) register_22 (
    .D(demultiplexer_1_out4), .en(\й4 ), .Q(register_22_q), .clk(and_21_out), .clr(clear));
  Register #(.width(16)) register_23 (
    .D(demultiplexer_1_out5), .en(\й5 ), .Q(register_23_q), .clk(and_22_out), .clr(clear));
  Register #(.width(16)) register_24 (
    .D(demultiplexer_1_out6), .en(\й6 ), .Q(register_24_q), .clk(and_23_out), .clr(clear));
  Register #(.width(16)) register_25 (
    .D(demultiplexer_1_out7), .en(\й7 ), .Q(register_25_q), .clk(and_24_out), .clr(clear));
  Register #(.width(16)) register_26 (
    .D(demultiplexer_1_out8), .en(\й8 ), .Q(register_26_q), .clk(and_25_out), .clr(clear));
  Register #(.width(16)) register_27 (
    .D(demultiplexer_1_out9), .en(\й9 ), .Q(register_27_q), .clk(and_26_out), .clr(clear));
  Register #(.width(16)) register_28 (
    .D(demultiplexer_1_out10), .en(\й10 ), .Q(register_28_q), .clk(and_27_out), .clr(clear));
  Register #(.width(16)) register_29 (
    .D(demultiplexer_1_out11), .en(\й11 ), .Q(register_29_q), .clk(and_28_out), .clr(clear));
  Register #(.width(16)) register_30 (
    .D(demultiplexer_1_out12), .en(\й12 ), .Q(register_30_q), .clk(and_29_out), .clr(clear));
  Register #(.width(16)) register_31 (
    .D(demultiplexer_1_out13), .en(\й13 ), .Q(register_31_q), .clk(and_30_out), .clr(clear));
  Register #(.width(16)) register_32 (
    .D(demultiplexer_1_out14), .en(\й14 ), .Q(register_32_q), .clk(and_31_out), .clr(clear));
  Register #(.width(16)) register_33 (
    .D(demultiplexer_1_out15), .en(\й15 ), .Q(register_33_q), .clk(and_32_out), .clr(clear));
  Multiplexer #(.width(16), .enable("false")) multiplexer_2 (.in0(_0), .in1(register_18_q), .out(out_6), .sel(\й0 ));
  Multiplexer #(.width(16), .enable("false")) multiplexer_3 (.in0(_1), .in1(register_19_q), .out(out_7), .sel(\й1 ));
  Multiplexer #(.width(16), .enable("false")) multiplexer_4 (.in0(_2), .in1(register_20_q), .out(out_8), .sel(\й2 ));
  Multiplexer #(.width(16), .enable("false")) multiplexer_5 (.in0(_3), .in1(register_21_q), .out(out_9), .sel(\й3 ));
  Multiplexer #(.width(16), .enable("false")) multiplexer_6 (.in0(_4), .in1(register_22_q), .out(out_10), .sel(\й4 ));
  Multiplexer #(.width(16), .enable("false")) multiplexer_7 (.in0(_5), .in1(register_23_q), .out(out_11), .sel(\й5 ));
  Multiplexer #(.width(16), .enable("false")) multiplexer_8 (.in0(_6), .in1(register_24_q), .out(out_12), .sel(\й6 ));
  Multiplexer #(.width(16), .enable("false")) multiplexer_9 (.in0(_7), .in1(register_25_q), .out(out_13), .sel(\й7 ));
  Multiplexer #(.width(16), .enable("false")) multiplexer_10 (.in0(_8), .in1(register_26_q), .out(out_14), .sel(\й8 ));
  Multiplexer #(.width(16), .enable("false")) multiplexer_11 (.in0(_9), .in1(register_27_q), .out(out_15), .sel(\й9 ));
  Multiplexer #(.width(16), .enable("false")) multiplexer_12 (
    .in0(_10), .in1(register_28_q), .out(out_16), .sel(\й10 ));
  Multiplexer #(.width(16), .enable("false")) multiplexer_13 (
    .in0(_11), .in1(register_29_q), .out(out_17), .sel(\й11 ));
  Multiplexer #(.width(16), .enable("false")) multiplexer_14 (
    .in0(_12), .in1(register_30_q), .out(out_18), .sel(\й12 ));
  Multiplexer #(.width(16), .enable("false")) multiplexer_15 (
    .in0(_13), .in1(register_31_q), .out(out_19), .sel(\й13 ));
  Multiplexer #(.width(16), .enable("false")) multiplexer_16 (
    .in0(_14), .in1(register_32_q), .out(out_20), .sel(\й14 ));
  Multiplexer #(.width(16), .enable("false")) multiplexer_17 (
    .in0(_15), .in1(register_33_q), .out(out_21), .sel(\й15 ));
endmodule
